# Fritzing sketch main (saved by Fritzing 0.9.2b)
breadboards: 1

parts:
  S1 = Round Pushbutton
  S2 = Round Pushbutton
  S3 = Round Pushbutton
  S4 = Round Pushbutton
  S6 = Round Pushbutton
  VCC1 = Battery block 9V
  S5 = Square Pushbutton
  R1 = Resistor [tolerance=±5% resistance=220 package="2512 [SMD]"]
  Part1 = Spark Core (v1.0)

nets:
  N1: S1.leg0, S2.leg0, S3.leg0, S4.leg0, S6.leg0, S5.leg0, R1.Pin_1, Part1.D0, Part1.D1, Part1.D2, Part1.D3, Part1.D4, Part1.D6
  N2: S1.leg1, S2.leg1, S3.leg1, S4.leg1, S6.leg1, S5.leg1, Part1.3V3
  N3: VCC1.-, R1.Pin_0, Part1.GND
  N4: VCC1.+, Part1.VIN

notes:
  Glass
  Plastic
  Cans
  Cups
  Milk
  MODE
